// Logisim project MIPS_MultiCycle.circ as structural Verilog
module main (
);

  wire [31:0] PC_q;

  Register #(.width(32)) PC (.Q(PC_q));  // open: D, en, clk, clr
  Multiplexer #(.enable("false"), .width(32)) multiplexer_1 (.in0(PC_q));  // open: in1, out, sel
  Memory memory_1 ();
  Register #(.width(32)) InstructionRegister ();  // open: D, en, clk, Q, clr
  Register #(.width(32)) MemoryDataRegister ();  // open: D, en, clk, Q, clr
  Control control_1 ();
  SignExtend signextend_1 ();
  Multiplexer #(.enable("false"), .width(32)) multiplexer_2 ();  // open: in0, in1, out, sel
  Multiplexer #(.enable("false"), .width(32)) multiplexer_3 ();  // open: in0, in1, out, sel
  Registers RegFile ();
  ShiftL2 shiftl2_1 ();
  Register #(.width(32)) A ();  // open: D, en, clk, Q, clr
  Register #(.width(32)) B ();  // open: D, en, clk, Q, clr
  ShiftL2 shiftl2_2 ();
  Multiplexer #(.enable("false"), .width(32)) multiplexer_4 ();  // open: in0, in1, out, sel
  Multiplexer #(.enable("false"), .select(2), .width(32)) multiplexer_5 ();  // open: in0, in1, in2, in3, out, sel
  ALU alu_1 ();
  Multiplexer #(.enable("false"), .select(2), .width(32)) multiplexer_6 ();  // open: in0, in1, in2, in3, out, sel
  ALU_Control alu_control_1 ();
  Register #(.width(32)) ALUOut ();  // open: D, en, clk, Q, clr
  Multiplexer #(.enable("false"), .width(32)) multiplexer_7 ();  // open: in0, in1, out, sel
  Register #(.width(32)) EPC ();  // open: D, en, clk, Q, clr
  Register #(.width(32)) Cause ();  // open: D, en, clk, Q, clr
endmodule
